# Fritzing sketch rgb_led_common_cathode (saved by Fritzing 0.9.9b)
breadboards: 2

parts:
  MCU1 = Raspberry Pi Zero
  R1 = Resistor [tolerance=±5% power=0.25 resistance=220 package=THT]
  R2 = Resistor [tolerance=±5% power=0.25 resistance=220 package=THT]
  R3 = Resistor [tolerance=±5% power=0.25 resistance=220 package=THT]
  LED2 = RGB LED (com. cathode, rbg) [package="5 mm [THT]"]
  R4 = Resistor [tolerance=±5% power=0.25 resistance=220 package=THT]  # not connected
  R5 = Resistor [tolerance=±5% power=0.25 resistance=220 package=THT]  # not connected
  R6 = Resistor [tolerance=±5% power=0.25 resistance=220 package=THT]  # not connected

nets:
  N1: MCU1.pin_6, MCU1.pin_34, LED2.common_cathode
  N2: MCU1.pin_11, R3.Pin_0
  N3: MCU1.pin_12, R1.Pin_0
  N4: MCU1.pin_13, R2.Pin_0
  N5: R1.Pin_1, LED2.red_anode
  N6: R2.Pin_1, LED2.green_anode
  N7: R3.Pin_1, LED2.blue_anode

notes:
  Physical arrangement
  Alternative view with parts removed to make circuit easier to see
